# Fritzing sketch switch_and_display_module (saved by Fritzing 1.0.5)
perfboards: 1

parts:
  R1 = Resistor [tolerance=±5% power=0.25W resistance=220 package=THT]
  R2 = Resistor [tolerance=±5% power=0.25W resistance=1k package=THT]
  R3 = Resistor [tolerance=±5% power=0.25W resistance=1k package=THT]
  R4 = Resistor [tolerance=±5% power=0.25W resistance=1k package=THT]
  R5 = Resistor [tolerance=±5% power=0.25W resistance=220 package=THT]
  R6 = Resistor [tolerance=±5% power=0.25W resistance=10k package=THT]
  R7 = Resistor [tolerance=±5% power=0.25W resistance=220 package=THT]
  R8 = Resistor [tolerance=±5% power=0.25W resistance=220 package=THT]
  R9 = Resistor [tolerance=±5% power=0.25W resistance=220 package=THT]
  R10 = Resistor [tolerance=±5% power=0.25W resistance=220 package=THT]
  R11 = Resistor [tolerance=±5% power=0.25W resistance=220 package=THT]
  R12 = Resistor [tolerance=±5% power=0.25W resistance=220 package=THT]
  R13 = Resistor [tolerance=±5% power=0.25W resistance=220 package=THT]
  R14 = Resistor [tolerance=±5% power=0.25W resistance=220 package=THT]
  R15 = Resistor [tolerance=±5% power=0.25W resistance=220 package=THT]
  R16 = Resistor [tolerance=±5% power=0.25W resistance=220 package=THT]  # not connected
  J1 = Camdenboss CTB0158-11 [part_number=CTB0158-11 package=THT]
  J2 = Camdenboss CTB0158-12 [part_number=CTB0158-12 package=THT]
  JP1 = Header 12 [package=1x12_machine-pin-header_lock.004]
  JP2 = Header 1 [package=1x01_offset]  # not connected
  JP3 = Header 1 [package=1x01_offset]  # not connected
  JP4 = Header 12 [package=1x12_machine-pin-header_lock.004]
  JP5 = Header 1 [package=1x01_offset]  # not connected
  JP6 = Header 1 [package=1x01_offset]  # not connected
  R17 = Resistor [tolerance=±5% power=0.25W resistance=220 package=THT]  # not connected

nets:
  N1: R1.Pin_0, JP1.3
  N2: R1.Pin_1, J1.pin3
  N3: R2.Pin_0, JP1.4
  N4: R2.Pin_1, J1.pin4
  N5: R3.Pin_0, JP1.5
  N6: R3.Pin_1, J1.pin5
  N7: R4.Pin_0, JP1.6
  N8: R4.Pin_1, J1.pin6
  N9: R5.Pin_0, JP1.9
  N10: R5.Pin_1, J1.pin9
  N11: R6.Pin_0, JP1.10
  N12: R6.Pin_1, J1.pin10
  N13: R7.Pin_0, JP4.2
  N14: R7.Pin_1, J2.pin2
  N15: R8.Pin_0, JP4.3
  N16: R8.Pin_1, J2.pin3
  N17: R9.Pin_1, J2.pin4
  N18: R10.Pin_1, J2.pin5
  N19: R11.Pin_1, J2.pin6
  N20: R12.Pin_1, J2.pin7
  N21: R13.Pin_1, J2.pin8
  N22: R14.Pin_1, J2.pin9
  N23: R15.Pin_1, J2.pin11
  N24: J1.pin1, JP1.1
  N25: J1.pin2, JP1.2
  N26: J1.pin7, JP1.7
  N27: J1.pin8, JP1.8
  N28: J1.pin11, JP4.1
